// Logisim project Trab5.circ as structural Verilog: 10 circuits, main circuit Trab4_Control
module Trab1 (
  input  [31:0] InputData,
  input  WriteEnable,
  input  Clock,
  input  Reset,
  output [31:0] OutputData,
  output [31:0] Instruction
);

  Register #(.width(32)) PC (.D(InputData), .en(WriteEnable), .clk(Clock), .Q(OutputData), .clr(Reset));
  ROM #(.addrWidth(24), .dataWidth(32)) rom_1 (.addr(OutputData[25:2]), .data(Instruction));

  // Notes on the sheet:
  //   contents of rom_1 (hex, n*v repeats v):
  //   430820 430821 430822 430823 20410001 8c410000 430824 430825 430827 30410001 34410001 14410011
  //   10410000 8c410000 24410001 ac410000 94410000 a4410000 90410000 a0410000 3c010000 400008 8000001
  //   c000003 16777180*0 5
endmodule

module Trab2_Registers (
  input  Clock,
  input  [31:0] WriteData,
  input  WriteEnable,
  input  [4:0] WriteRegister,
  input  [4:0] ReadRegister1,
  input  [4:0] ReadRegister2,
  output [31:0] ReadData1,
  output [31:0] ReadData2
);

  wire demultiplexer_1_out0, demultiplexer_1_out1, demultiplexer_1_out2, demultiplexer_1_out3,
       demultiplexer_1_out4, demultiplexer_1_out5, demultiplexer_1_out6, demultiplexer_1_out7,
       demultiplexer_1_out8, demultiplexer_1_out9, demultiplexer_1_out10, demultiplexer_1_out11,
       demultiplexer_1_out12, demultiplexer_1_out13, demultiplexer_1_out14, demultiplexer_1_out15,
       demultiplexer_1_out16, demultiplexer_1_out17, demultiplexer_1_out18, demultiplexer_1_out19,
       demultiplexer_1_out20, demultiplexer_1_out21, demultiplexer_1_out22, demultiplexer_1_out23,
       demultiplexer_1_out24, demultiplexer_1_out25, demultiplexer_1_out26, demultiplexer_1_out27,
       demultiplexer_1_out28, demultiplexer_1_out29, demultiplexer_1_out30, demultiplexer_1_out31;
  wire [31:0] register_1_q, register_2_q, register_3_q, register_4_q, register_5_q, register_6_q,
       register_7_q, register_8_q, register_9_q, register_10_q, register_11_q, register_12_q, register_13_q,
       register_14_q, register_15_q, register_16_q, register_17_q, register_18_q, register_19_q,
       register_20_q, register_21_q, register_22_q, register_23_q, register_24_q, register_25_q,
       register_26_q, register_27_q, register_28_q, register_29_q, register_30_q, register_31_q,
       register_32_q;

  Demultiplexer #(.select(5), .enable("false")) demultiplexer_1 (
    .out0(demultiplexer_1_out0), .out1(demultiplexer_1_out1), .out2(demultiplexer_1_out2),
    .out3(demultiplexer_1_out3), .out4(demultiplexer_1_out4), .out5(demultiplexer_1_out5),
    .out6(demultiplexer_1_out6), .out7(demultiplexer_1_out7), .out8(demultiplexer_1_out8),
    .out9(demultiplexer_1_out9), .out10(demultiplexer_1_out10), .out11(demultiplexer_1_out11),
    .out12(demultiplexer_1_out12), .out13(demultiplexer_1_out13), .out14(demultiplexer_1_out14),
    .out15(demultiplexer_1_out15), .out16(demultiplexer_1_out16), .out17(demultiplexer_1_out17),
    .out18(demultiplexer_1_out18), .out19(demultiplexer_1_out19), .out20(demultiplexer_1_out20),
    .out21(demultiplexer_1_out21), .out22(demultiplexer_1_out22), .out23(demultiplexer_1_out23),
    .out24(demultiplexer_1_out24), .out25(demultiplexer_1_out25), .out26(demultiplexer_1_out26),
    .out27(demultiplexer_1_out27), .out28(demultiplexer_1_out28), .out29(demultiplexer_1_out29),
    .out30(demultiplexer_1_out30), .out31(demultiplexer_1_out31), .in(WriteEnable), .sel(WriteRegister));
  Register #(.width(32)) register_1 (
    .D(WriteData), .en(demultiplexer_1_out0), .clk(Clock), .Q(register_1_q), .clr(1'b1));
  Register #(.width(32)) register_2 (
    .D(WriteData), .en(demultiplexer_1_out1), .clk(Clock), .Q(register_2_q), .clr(1'b0));
  Register #(.width(32)) register_3 (
    .D(WriteData), .en(demultiplexer_1_out2), .clk(Clock), .Q(register_3_q), .clr(1'b0));
  Register #(.width(32)) register_4 (
    .D(WriteData), .en(demultiplexer_1_out3), .clk(Clock), .Q(register_4_q), .clr(1'b0));
  Register #(.width(32)) register_5 (
    .D(WriteData), .en(demultiplexer_1_out4), .clk(Clock), .Q(register_5_q), .clr(1'b0));
  Register #(.width(32)) register_6 (
    .D(WriteData), .en(demultiplexer_1_out5), .clk(Clock), .Q(register_6_q), .clr(1'b0));
  Register #(.width(32)) register_7 (
    .D(WriteData), .en(demultiplexer_1_out6), .clk(Clock), .Q(register_7_q), .clr(1'b0));
  Register #(.width(32)) register_8 (
    .D(WriteData), .en(demultiplexer_1_out7), .clk(Clock), .Q(register_8_q), .clr(1'b0));
  Register #(.width(32)) register_9 (
    .D(WriteData), .en(demultiplexer_1_out8), .clk(Clock), .Q(register_9_q), .clr(1'b0));
  Register #(.width(32)) register_10 (
    .D(WriteData), .en(demultiplexer_1_out9), .clk(Clock), .Q(register_10_q), .clr(1'b0));
  Register #(.width(32)) register_11 (
    .D(WriteData), .en(demultiplexer_1_out10), .clk(Clock), .Q(register_11_q), .clr(1'b0));
  Register #(.width(32)) register_12 (
    .D(WriteData), .en(demultiplexer_1_out11), .clk(Clock), .Q(register_12_q), .clr(1'b0));
  Register #(.width(32)) register_13 (
    .D(WriteData), .en(demultiplexer_1_out12), .clk(Clock), .Q(register_13_q), .clr(1'b0));
  Register #(.width(32)) register_14 (
    .D(WriteData), .en(demultiplexer_1_out13), .clk(Clock), .Q(register_14_q), .clr(1'b0));
  Register #(.width(32)) register_15 (
    .D(WriteData), .en(demultiplexer_1_out14), .clk(Clock), .Q(register_15_q), .clr(1'b0));
  Register #(.width(32)) register_16 (
    .D(WriteData), .en(demultiplexer_1_out15), .clk(Clock), .Q(register_16_q), .clr(1'b0));
  Register #(.width(32)) register_17 (
    .D(WriteData), .en(demultiplexer_1_out16), .clk(Clock), .Q(register_17_q), .clr(1'b0));
  Register #(.width(32)) register_18 (
    .D(WriteData), .en(demultiplexer_1_out17), .Q(register_18_q), .clr(1'b0));  // open: clk
  Register #(.width(32)) register_19 (
    .D(WriteData), .en(demultiplexer_1_out18), .clk(Clock), .Q(register_19_q), .clr(1'b0));
  Register #(.width(32)) register_20 (
    .D(WriteData), .en(demultiplexer_1_out19), .clk(Clock), .Q(register_20_q), .clr(1'b0));
  Register #(.width(32)) register_21 (
    .D(WriteData), .en(demultiplexer_1_out29), .clk(Clock), .Q(register_21_q), .clr(1'b0));
  Register #(.width(32)) register_22 (
    .D(WriteData), .en(demultiplexer_1_out20), .clk(Clock), .Q(register_22_q), .clr(1'b0));
  Register #(.width(32)) register_23 (
    .D(WriteData), .en(demultiplexer_1_out21), .clk(Clock), .Q(register_23_q), .clr(1'b0));
  Register #(.width(32)) register_24 (
    .D(WriteData), .en(demultiplexer_1_out22), .clk(Clock), .Q(register_24_q), .clr(1'b0));
  Register #(.width(32)) register_25 (
    .D(WriteData), .en(demultiplexer_1_out23), .clk(Clock), .Q(register_25_q), .clr(1'b0));
  Register #(.width(32)) register_26 (
    .D(WriteData), .en(demultiplexer_1_out24), .clk(Clock), .Q(register_26_q), .clr(1'b0));
  Register #(.width(32)) register_27 (
    .D(WriteData), .en(demultiplexer_1_out25), .clk(Clock), .Q(register_27_q), .clr(1'b0));
  Register #(.width(32)) register_28 (
    .D(WriteData), .en(demultiplexer_1_out26), .clk(Clock), .Q(register_28_q), .clr(1'b0));
  Register #(.width(32)) register_29 (
    .D(WriteData), .en(demultiplexer_1_out27), .clk(Clock), .Q(register_29_q), .clr(1'b0));
  Register #(.width(32)) register_30 (
    .D(WriteData), .en(demultiplexer_1_out28), .clk(Clock), .Q(register_30_q), .clr(1'b0));
  Register #(.width(32)) register_31 (
    .D(WriteData), .en(demultiplexer_1_out30), .clk(Clock), .Q(register_31_q), .clr(1'b0));
  Register #(.width(32)) register_32 (
    .D(WriteData), .en(demultiplexer_1_out31), .clk(Clock), .Q(register_32_q), .clr(1'b0));
  Multiplexer #(.select(5), .width(32), .enable("false")) multiplexer_1 (
    .in0(register_1_q), .in1(register_2_q), .in2(register_3_q), .in3(register_4_q), .in4(register_5_q),
    .in5(register_6_q), .in6(register_7_q), .in7(register_8_q), .in8(register_9_q), .in9(register_10_q),
    .in10(register_11_q), .in11(register_12_q), .in12(register_13_q), .in13(register_14_q),
    .in14(register_15_q), .in15(register_16_q), .in16(register_17_q), .in17(register_18_q),
    .in18(register_19_q), .in19(register_20_q), .in20(register_21_q), .in21(register_22_q),
    .in22(register_23_q), .in23(register_24_q), .in24(register_25_q), .in25(register_26_q),
    .in26(register_27_q), .in27(register_28_q), .in28(register_29_q), .in29(register_30_q),
    .in30(register_31_q), .in31(register_32_q), .out(ReadData1), .sel(ReadRegister1));
  Multiplexer #(.select(5), .width(32), .enable("false")) multiplexer_2 (
    .in0(register_1_q), .in1(register_2_q), .in2(register_3_q), .in3(register_4_q), .in4(register_5_q),
    .in5(register_6_q), .in6(register_7_q), .in7(register_8_q), .in8(register_9_q), .in9(register_10_q),
    .in10(register_11_q), .in11(register_12_q), .in12(register_13_q), .in13(register_14_q),
    .in14(register_15_q), .in15(register_16_q), .in16(register_17_q), .in17(register_18_q),
    .in18(register_19_q), .in19(register_20_q), .in20(register_21_q), .in21(register_22_q),
    .in22(register_23_q), .in23(register_24_q), .in24(register_25_q), .in25(register_26_q),
    .in26(register_27_q), .in27(register_28_q), .in28(register_29_q), .in29(register_30_q),
    .in30(register_31_q), .in31(register_32_q), .out(ReadData2), .sel(ReadRegister2));
endmodule

module Trab2_ALU (
  input  [31:0] Input1,
  input  [31:0] Input2,
  input  [3:0] ALU_Control,
  output [31:0] ALU_Result,
  output out_5
);

  wire comparator_1_eq, or_2_out;
  wire [31:0] adder_1_out, and_1_out, bit_extender_1_out, nor_1_out, or_1_out, subtractor_1_out;

  Adder #(.width(32)) adder_1 (.a(Input1), .b(Input2), .out(adder_1_out), .cin(1'b0));  // open: cout
  Subtractor #(.width(32)) subtractor_1 (.a(Input1), .b(Input2), .out(subtractor_1_out), .bin(1'b0));  // open: bout
  assign and_1_out = Input1 & Input2;  // AND_Gate and_1, 32 bits wide
  assign or_1_out = Input1 | Input2;  // OR_Gate or_1, 32 bits wide
  Comparator #(.width(32)) comparator_1 (.a(Input1), .b(Input2), .eq(comparator_1_eq));  // open: gt, lt
  assign nor_1_out = ~(Input1 | Input2);  // NOR_Gate nor_1, 32 bits wide
  assign bit_extender_1_out = {{31{comparator_1_eq}}, comparator_1_eq};  // Bit_Extender bit_extender_1
  Multiplexer #(.select(4), .width(32), .enable("false")) multiplexer_1 (
    .in0(adder_1_out), .in1(adder_1_out), .in2(subtractor_1_out), .in3(subtractor_1_out), .in4(and_1_out),
    .in5(or_1_out), .in6(nor_1_out), .in7(nor_1_out), .in8(bit_extender_1_out), .in15(32'h1),
    .out(ALU_Result), .sel(ALU_Control));  // open: in9, in10, in11, in12, in13, in14
  or or_2 (or_2_out, ALU_Result[0], ALU_Result[1], ALU_Result[2], ALU_Result[3], ALU_Result[4], ALU_Result[5], ALU_Result[6], ALU_Result[7], ALU_Result[8], ALU_Result[9], ALU_Result[10], ALU_Result[11], ALU_Result[12], ALU_Result[13], ALU_Result[14], ALU_Result[15], ALU_Result[17], ALU_Result[18], ALU_Result[19], ALU_Result[20], ALU_Result[21], ALU_Result[22], ALU_Result[23], ALU_Result[24], ALU_Result[25], ALU_Result[26], ALU_Result[27], ALU_Result[28], ALU_Result[29], ALU_Result[30], ALU_Result[31], ALU_Result[16]);
  not not_1 (out_5, or_2_out);
endmodule

module Trab3_SignExtend (
  input  [15:0] Input_16,
  output [31:0] Output_32
);


  assign Output_32 = {{17{Input_16[15]}}, Input_16[14:0]};
endmodule

module Trab3_Shift_Left_2 (
  input  [31:0] InputData,
  output [31:0] OutputData
);


  assign OutputData = {InputData[29:0], 2'b00};
endmodule

module Trab3_Data_Memory (
  input  [31:0] Address,
  input  [31:0] WriteData,
  input  [1:0] WordHalfByte,
  input  MemoryWrite,
  input  MemoryRead,
  input  Clock,
  output [31:0] ReadData
);

  wire [1:0] demultiplexer_2_out0, demultiplexer_2_out1;
  wire [3:0] demultiplexer_1_out0, multiplexer_1_out;
  wire [7:0] demultiplexer_4_out0, demultiplexer_4_out1, demultiplexer_4_out2, demultiplexer_4_out3,
       multiplexer_4_out;
  wire [15:0] demultiplexer_3_out0, demultiplexer_3_out1, multiplexer_3_out;
  wire [31:0] multiplexer_2_out, ram_1_dout;

  Demultiplexer #(.select(2), .enable("false")) demultiplexer_1 (
    .out0(demultiplexer_1_out0[0]), .out1(demultiplexer_1_out0[1]), .out2(demultiplexer_1_out0[2]),
    .out3(demultiplexer_1_out0[3]), .in(MemoryWrite), .sel(Address[1:0]));
  Demultiplexer #(.width(2), .enable("false")) demultiplexer_2 (
    .out0(demultiplexer_2_out0), .out1(demultiplexer_2_out1), .in({2{MemoryWrite}}), .sel(Address[1]));
  Demultiplexer #(.width(16), .enable("false")) demultiplexer_3 (
    .out0(demultiplexer_3_out0), .out1(demultiplexer_3_out1), .in(WriteData[15:0]), .sel(Address[1]));
  Demultiplexer #(.select(2), .width(8), .enable("false")) demultiplexer_4 (
    .out0(demultiplexer_4_out0), .out1(demultiplexer_4_out1), .out2(demultiplexer_4_out2),
    .out3(demultiplexer_4_out3), .in(WriteData[7:0]), .sel(Address[1:0]));
  Multiplexer #(.select(2), .width(4), .enable("false")) multiplexer_1 (
    .in0({4{MemoryWrite}}), .in1({demultiplexer_2_out1, demultiplexer_2_out0}), .in2(demultiplexer_1_out0),
    .in3(4'b0000), .out(multiplexer_1_out), .sel(WordHalfByte));
  Multiplexer #(.select(2), .width(32), .enable("false")) multiplexer_2 (
    .in0(WriteData), .in1({demultiplexer_3_out1, demultiplexer_3_out0}),
    .in2({demultiplexer_4_out3, demultiplexer_4_out2, demultiplexer_4_out1, demultiplexer_4_out0}),
    .in3({32{1'b0}}), .out(multiplexer_2_out), .sel(WordHalfByte));
  RAM #(.addrWidth(24), .databus("bibus")) ram_1 (
    .addr(Address[25:2]), .we(multiplexer_1_out[0]), .oe(MemoryRead), .clk(Clock),
    .din(multiplexer_2_out[7:0]), .dout(ram_1_dout[7:0]));
  RAM #(.addrWidth(24), .databus("bibus")) ram_2 (
    .addr(Address[25:2]), .we(multiplexer_1_out[1]), .oe(MemoryRead), .clk(Clock),
    .din(multiplexer_2_out[15:8]), .dout(ram_1_dout[15:8]));
  RAM #(.addrWidth(24), .databus("bibus")) ram_3 (
    .addr(Address[25:2]), .we(multiplexer_1_out[2]), .oe(MemoryRead), .clk(Clock),
    .din(multiplexer_2_out[23:16]), .dout(ram_1_dout[23:16]));
  RAM #(.addrWidth(24), .databus("bibus")) ram_4 (
    .addr(Address[25:2]), .we(multiplexer_1_out[3]), .oe(MemoryRead), .clk(Clock),
    .din(multiplexer_2_out[31:24]), .dout(ram_1_dout[31:24]));
  Multiplexer #(.width(16), .enable("false")) multiplexer_3 (
    .in0(ram_1_dout[15:0]), .in1(ram_1_dout[31:16]), .out(multiplexer_3_out), .sel(Address[1]));
  Multiplexer #(.select(2), .width(8), .enable("false")) multiplexer_4 (
    .in0(ram_1_dout[7:0]), .in1(ram_1_dout[15:8]), .in2(ram_1_dout[23:16]), .in3(ram_1_dout[31:24]),
    .out(multiplexer_4_out), .sel(WordHalfByte));
  Multiplexer #(.select(2), .width(32), .enable("false")) multiplexer_5 (
    .in0(ram_1_dout), .in1({{16{1'b0}}, multiplexer_3_out}), .in2({{24{1'b0}}, multiplexer_4_out}),
    .in3({32{1'b0}}), .out(ReadData), .sel(WordHalfByte));

  // Other names for the same wires on the sheet: MW = MemoryWrite; WD[31:0] = WriteData; A0 = Address[0];
  //   A1 = Address[1]; A[23:0] = Address[25:2]; WHB[1:0] = WordHalfByte
endmodule

module Trab3 (
  input  Write,
  input  Clock,
  input  Reset,
  input  [1:0] WordHalfByte,
  output [31:0] ALU_Input_1,
  output [31:0] ALU_Result,
  output [31:0] ALU_Input_2,
  output [4:0] out_8,
  output [4:0] out_9
);

  wire ALU_SRC, Branch, Jal, Jump, JumptoRegister, MR, MTR, MW, PC_SRC, RegDst, RW, trab2_alu_1_out_5;
  wire [2:0] trab4_control_1_alu_op;
  wire [3:0] ALU_OP;
  wire [4:0] multiplexer_1_out, multiplexer_2_out;
  wire [5:0] ALU_Instruction;
  wire [31:0] adder_1_out, adder_2_out, multiplexer_3_out, multiplexer_5_out, multiplexer_6_out,
       multiplexer_7_out, multiplexer_8_out, shifter_1_out, SignExtended, trab1_1_outputdata,
       trab3_data_memory_1_readdata, trab5_instruction_1_target, WriteData;
  wire [31:6] trab1_1_instruction;

  Trab1 trab1_1 (
    .InputData(multiplexer_3_out), .WriteEnable(Write), .Clock(Clock), .Reset(Reset),
    .OutputData(trab1_1_outputdata),
    .Instruction({trab1_1_instruction[31:26], out_8, out_9, trab1_1_instruction[15:6], ALU_Instruction}));
  Multiplexer #(.width(5), .enable("false")) multiplexer_1 (
    .in0(out_9), .in1(trab1_1_instruction[15:11]), .out(multiplexer_1_out), .sel(RegDst));
  Multiplexer #(.width(5), .enable("false")) multiplexer_2 (
    .in0(multiplexer_1_out), .in1({5{1'b1}}), .out(multiplexer_2_out), .sel(Jal));
  Trab3_SignExtend trab3_signextend_1 (
    .Input_16({trab1_1_instruction[15:6], ALU_Instruction}), .Output_32(SignExtended));
  Adder #(.width(32)) adder_1 (.a(trab1_1_outputdata), .b(32'h4), .out(adder_1_out), .cin(1'b0));  // open: cout
  Trab4_Control trab4_control_1 (
    .Instruction(trab1_1_instruction[31:26]), .RegDst(RegDst), .Branch(Branch), .MemoryRead(MR),
    .MemToReg(MTR), .ALU_OP(trab4_control_1_alu_op), .MemWrite(MW), .ALU_SRC(ALU_SRC), .RegisterWrite(RW),
    .WHB(WordHalfByte), .Jump(Jump), .out_12(Jal));
  Multiplexer #(.width(32), .enable("false")) multiplexer_3 (
    .in0(multiplexer_6_out), .in1(trab5_instruction_1_target), .out(multiplexer_3_out), .sel(JumptoRegister));
  Trab5_Instruction trab5_instruction_1 (
    .Instruction({trab1_1_instruction[31:26], out_8, out_9, trab1_1_instruction[15:6], ALU_Instruction}),
    .PC(adder_1_out), .Target(trab5_instruction_1_target));
  Trab2_Registers trab2_registers_1 (
    .ReadData1(ALU_Input_1), .ReadRegister1(out_8), .WriteEnable(RW), .Clock(Clock),
    .WriteData(multiplexer_8_out), .WriteRegister(multiplexer_2_out), .ReadRegister2(out_9),
    .ReadData2(WriteData));
  Multiplexer #(.width(32), .enable("false")) multiplexer_4 (
    .in0(WriteData), .in1(SignExtended), .out(ALU_Input_2), .sel(ALU_SRC));
  Shifter #(.width(32)) shifter_1 (.in(SignExtended), .\dist (5'b00010), .out(shifter_1_out));
  Adder #(.width(32)) adder_2 (.a(adder_1_out), .b(shifter_1_out), .out(adder_2_out), .cin(1'b0));  // open: cout
  Multiplexer #(.width(32), .enable("false")) multiplexer_5 (
    .in0(adder_1_out), .in1(adder_2_out), .out(multiplexer_5_out), .sel(PC_SRC));
  Trab2_ALU trab2_alu_1 (
    .Input1(ALU_Input_1), .Input2(ALU_Input_2), .ALU_Control(ALU_OP), .ALU_Result(ALU_Result),
    .out_5(trab2_alu_1_out_5));
  and and_1 (PC_SRC, trab2_alu_1_out_5, Branch);
  Multiplexer #(.width(32), .enable("false")) multiplexer_6 (
    .in0(multiplexer_5_out), .in1(trab5_instruction_1_target), .out(multiplexer_6_out), .sel(Jump));
  Trab4_ALU_Control trab4_alu_control_1 (
    .ALU_Instruction(ALU_Instruction), .ALU_OP(trab4_control_1_alu_op), .ALU_Control(ALU_OP),
    .JumpToRegisters(JumptoRegister));
  Multiplexer #(.width(32), .enable("false")) multiplexer_7 (
    .in0(ALU_Result), .in1(trab3_data_memory_1_readdata), .out(multiplexer_7_out), .sel(MTR));
  Trab3_Data_Memory trab3_data_memory_1 (
    .Address(ALU_Result), .WriteData(WriteData), .WordHalfByte(WordHalfByte), .MemoryWrite(MW),
    .MemoryRead(MR), .Clock(Clock), .ReadData(trab3_data_memory_1_readdata));
  Multiplexer #(.width(32), .enable("false")) multiplexer_8 (
    .in0(multiplexer_7_out), .in1(adder_1_out), .out(multiplexer_8_out), .sel(Jal));

  // Other names for the same wires on the sheet: RR2[4:0] = out_9; RR1[4:0] = out_8; WHB[1:0] = WordHalfByte
endmodule

module Trab4_Control (
  input  [5:0] Instruction,
  output RegDst,
  output Branch,
  output MemoryRead,
  output MemToReg,
  output [2:0] ALU_OP,
  output MemWrite,
  output ALU_SRC,
  output RegisterWrite,
  output [1:0] WHB,
  output Jump,
  output out_12
);

  wire [15:14] rom_1_data;

  ROM #(.addrWidth(6), .dataWidth(16)) rom_1 (
    .addr(Instruction),
    .data({rom_1_data, out_12, Jump, WHB, RegisterWrite, ALU_SRC, MemWrite, ALU_OP, MemToReg, MemoryRead, Branch, RegDst}));

  // Notes on the sheet:
  //   contents of rom_1 (hex, n*v repeats v):
  //   201 215 10 2 0 52 10 0 314 314 0 0 324 334 241 17*0 81c 71c 0 314 81c 71c 0 0 990 590 0 190
endmodule

module Trab4_ALU_Control (
  input  [5:0] ALU_Instruction,
  input  [2:0] ALU_OP,
  output [3:0] ALU_Control,
  output JumpToRegisters
);

  wire comparator_1_eq, comparator_2_eq;

  Multiplexer #(.select(3), .width(4), .enable("false")) multiplexer_1 (
    .in0(ALU_Instruction[3:0]), .in1(4'b0000), .in2(4'b0100), .in3(4'b0101), .in4(4'b0011), .in5(4'b0011),
    .out(ALU_Control), .sel(ALU_OP));  // open: in6, in7
  Comparator #(.width(3)) comparator_1 (.a(ALU_OP), .b(3'b000), .eq(comparator_1_eq));  // open: gt, lt
  Comparator #(.width(6)) comparator_2 (.a(6'b001000), .b(ALU_Instruction), .eq(comparator_2_eq));  // open: gt, lt
  and and_1 (JumpToRegisters, comparator_1_eq, comparator_2_eq);
endmodule

module Trab5_Instruction (
  input  [31:0] Instruction,
  input  [31:0] PC,
  output [31:0] Target
);


  assign Target = {PC[31:28], Instruction[25:0], 2'b00};
endmodule
