// Logisim project lab31.circ as structural Verilog: 1 circuit, main circuit main
module main (
  input  A1,
  input  A0,
  input  [1:0] WriteHalfByte,
  input  [31:0] WriteData,
  input  MemoryWrite,
  input  [31:0] Address,
  input  MemoryRead,
  input  Clock
);

  wire [1:0] demultiplexer_1_out0, demultiplexer_1_out1;
  wire [3:0] demultiplexer_2_out0, multiplexer_1_out;
  wire [7:0] demultiplexer_4_out0, demultiplexer_4_out1, demultiplexer_4_out2, demultiplexer_4_out3;
  wire [15:0] demultiplexer_3_out0, demultiplexer_3_out1, multiplexer_3_out;
  wire [31:0] multiplexer_2_out, ram_1_dout;

  Demultiplexer #(.width(2), .enable("false")) demultiplexer_1 (
    .out0(demultiplexer_1_out0), .out1(demultiplexer_1_out1), .in({2{MemoryWrite}}), .sel(A1));
  Demultiplexer #(.select(2), .enable("false")) demultiplexer_2 (
    .out0(demultiplexer_2_out0[0]), .out1(demultiplexer_2_out0[1]), .out2(demultiplexer_2_out0[2]),
    .out3(demultiplexer_2_out0[3]), .in(MemoryWrite), .sel({A1, A0}));
  Demultiplexer #(.width(16), .enable("false")) demultiplexer_3 (
    .out0(demultiplexer_3_out0), .out1(demultiplexer_3_out1), .in(WriteData[15:0]), .sel(A1));
  Demultiplexer #(.select(2), .width(8), .enable("false")) demultiplexer_4 (
    .out0(demultiplexer_4_out0), .out1(demultiplexer_4_out1), .out2(demultiplexer_4_out2),
    .out3(demultiplexer_4_out3), .in(WriteData[7:0]), .sel({A1, A0}));
  Multiplexer #(.select(2), .width(4), .enable("false")) multiplexer_1 (
    .in0({4{MemoryWrite}}), .in1({demultiplexer_1_out1, demultiplexer_1_out0}), .in2(demultiplexer_2_out0),
    .in3(4'b0000), .out(multiplexer_1_out), .sel(WriteHalfByte));
  Multiplexer #(.select(2), .width(32), .enable("false")) multiplexer_2 (
    .in0(WriteData), .in1({demultiplexer_3_out1, demultiplexer_3_out0}),
    .in2({demultiplexer_4_out3, demultiplexer_4_out2, demultiplexer_4_out1, demultiplexer_4_out0}),
    .in3({32{1'b0}}), .out(multiplexer_2_out), .sel(WriteHalfByte));
  RAM #(.addrWidth(24), .databus("bibus")) ram_1 (
    .addr(Address[25:2]), .we(multiplexer_1_out[0]), .oe(MemoryRead), .clk(Clock),
    .din(multiplexer_2_out[7:0]), .dout(ram_1_dout[7:0]));
  RAM #(.addrWidth(24), .databus("bibus")) ram_2 (
    .addr(Address[25:2]), .we(multiplexer_1_out[1]), .oe(MemoryRead), .clk(Clock),
    .din(multiplexer_2_out[15:8]), .dout(ram_1_dout[15:8]));
  RAM #(.addrWidth(24), .databus("bibus")) ram_3 (
    .addr(Address[25:2]), .we(multiplexer_1_out[2]), .oe(MemoryRead), .clk(Clock),
    .din(multiplexer_2_out[23:16]), .dout(ram_1_dout[23:16]));
  RAM #(.addrWidth(24), .databus("bibus")) ram_4 (
    .addr(Address[25:2]), .we(multiplexer_1_out[3]), .oe(MemoryRead), .clk(Clock),
    .din(multiplexer_2_out[31:24]), .dout(ram_1_dout[31:24]));
  Multiplexer #(.width(16), .enable("false")) multiplexer_3 (
    .in0(ram_1_dout[15:0]), .in1(ram_1_dout[31:16]), .out(multiplexer_3_out), .sel(Address[1]));
  Multiplexer #(.select(2), .width(32), .enable("false")) multiplexer_4 (
    .in0(ram_1_dout), .in1({{16{1'b0}}, multiplexer_3_out}), .sel(WriteHalfByte));  // open: in2, in3, out
endmodule
